# Fritzing sketch sketch_pump (saved by Fritzing 0.9.3b)
breadboards: 1

parts:
  Raspberry_Pi_1 = Raspberry Pi 3 [part_number=RPI-3-V1.2]
  DS2Y-5-DC5V1 = DS2Y-5-DC5V [part_number=DS2Y-5-DC5V]
  M1 = DC Motor
  R1 = Resistor [tolerance=±5% resistance=220 package="0402 [SMD]"]
  U1 = DIODE-ZENER [package=diode-zener]
  Q1 = TRANSISTOR_NPN [package=to-92-ammo]

nets:
  N1: Raspberry_Pi_1.GPIO4, Q1.B
  N2: Raspberry_Pi_1.GND, Q1.E
  N3: Raspberry_Pi_1.5V, DS2Y-5-DC5V1.16_-, U1.C
  N4: DS2Y-5-DC5V1.1_+, U1.A, Q1.C
  N5: DS2Y-5-DC5V1.11_N.C., R1.Pin_0
  N6: DS2Y-5-DC5V1.9_N.O., M1.pin_2
  N7: M1.pin_1, R1.Pin_1

notes:
  Power 12V DC
  Pump 12V DC
